# Fritzing sketch victoria (saved by Fritzing 0.9.2b)
circuit board: 8.46667cm x 5.64444cm
breadboards: 1

parts:
  Part1 = Arduino Mega 2560 (Rev3)
  Q2 = Basic FET N-Channel [package="TO220 [THT]"]
  R1 = Resistor [tolerance=±5% resistance=100 package=THT]
  R2 = Resistor [tolerance=±5% resistance=10k package=THT]
  J1 = double row male pin header, 6 pins [form="♂ (male)"]
  JP1 = Header 2 [package=screwterminal-3.5mm-2_lock]

nets:
  N1: Part1.D21/SCL, J1.pin6
  N2: Part1.D20/SDA, J1.pin5
  N3: Part1.D15/RX3, J1.pin2
  N4: Part1.D14/TX3, J1.pin3
  N5: Part1.GND, Q2.source, R2.Pin_1, JP1.2
  N6: Part1.VIN, J1.pin1, JP1.1
  N7: Part1.D24, R1.Pin_0
  N8: Q2.gate, R1.Pin_1, R2.Pin_0
  N9: Q2.drain, J1.pin4
